# Fritzing sketch human_circuit (saved by Fritzing 1.0.4)
breadboards: 1

parts:
  A1 = Arduino Nano Every THT
  +9V_Supply = 2.1mm Barrel Jack with Terminal Block
  A2 = 2 channel relay module [package=THT]
  Threshold_Pots = Rotary Potentiometer (Large) [maximum_resistance=10kΩ knob_status=50% power=0.5W package=THT]
  R2 = Rotary Potentiometer (Large) [maximum_resistance=10kΩ knob_status=50% power=0.5W package=THT]
  R3 = Rotary Potentiometer (Large) [maximum_resistance=10kΩ knob_status=50% power=0.5W package=THT]
  LED2 = LED - 3mm [color="Green (565nm)" current=0.030A package="3 mm [THT]"]
  LED3 = LED - 3mm [color="Red (633nm)" current=0.030A package="3 mm [THT]"]
  LCD2004_I2C = LCD2004-I2C
  LED1 = LED - 3mm [color="Green (560nm)" current=0.030A package="3 mm [THT]"]
  J1 = female pin header, 1 pin [form="♀ (female)"]
  J2 = female pin header, 1 pin [form="♀ (female)"]
  Cap_Sense_Resistors = Resistor [tolerance=±1% power=0.25W resistance=1M package=THT]
  R5 = Resistor [tolerance=±1% power=0.25W resistance=1M package=THT]
  R9 = Resistor [tolerance=±1% power=0.25W resistance=1M package=THT]
  R10 = Resistor [tolerance=±1% power=0.25W resistance=1k package=THT]
  C1 = Electrolytic Capacitor [capacitance=0.47µ voltage=35V package="100 mil [THT, electrolytic]"]
  R8 = Resistor [tolerance=±5% power=0.25W resistance=330 package=THT]
  R7 = Resistor [tolerance=±5% power=0.25W resistance=330 package=THT]
  LED_Pulldowns = Resistor [tolerance=±5% power=0.25W resistance=330 package=THT]
  R11 = Resistor [tolerance=±1% power=0.25W resistance=1k package=THT]

nets:
  N1: A1.Pin_4, Threshold_Pots.wiper
  N2: A1.Pin_5, R3.wiper
  N3: A1.Pin_6, R2.wiper
  N4: A1.Pin_8, LCD2004_I2C.SDA
  N5: A1.Pin_9, LCD2004_I2C.SCL
  N6: A1.Pin_11, R10.Pin_0, C1.+
  N7: A1.Pin_12, A2.pin_13, Threshold_Pots.leg2, R2.leg2, R3.leg2, LCD2004_I2C.VCC, R9.Pin_1
  N8: A1.Pin_13, A1.Pin_18
  N9: A1.Pin_14, A1.Pin_19, +9V_Supply.NEG, A2.pin_14, Threshold_Pots.leg1, R2.leg1, R3.leg1, LCD2004_I2C.GND, C1.-, R8.Pin_0, R7.Pin_0, LED_Pulldowns.Pin_0, R11.Pin_1
  N10: A1.Pin_15, +9V_Supply.POS
  N11: A1.Pin_20, LED3.anode
  N12: A1.Pin_21, LED2.anode
  N13: A1.Pin_22, LED1.anode
  N14: A1.Pin_23, A2.pin_6, R5.Pin_0
  N15: A1.Pin_25, Cap_Sense_Resistors.Pin_1, R5.Pin_1
  N16: A1.Pin_27, A2.pin_3, Cap_Sense_Resistors.Pin_0
  N17: A1.Pin_29, A2.pin_16
  N18: A1.Pin_30, A2.pin_15
  N19: A2.pin_1, R9.Pin_0, R10.Pin_1
  N20: A2.pin_2, J1.pin1
  N21: A2.pin_4, R11.Pin_0
  N22: A2.pin_5, J2.pin1
  N23: LED2.cathode, R7.Pin_1
  N24: LED3.cathode, LED_Pulldowns.Pin_1
  N25: LED1.cathode, R8.Pin_1

notes:
  Left Hand
  Right Hand
  Blue = Impedence Sense Circuit
  Human Circuit Sensing Module

custom parts:
  Arduino Nano Every THT: The Nano Every is Arduino’s 5V compatible board in the smallest available form factor: 45x18mm! The Arduino Nano is the preferred board for many projects requiring a small and easy to use microcontroller board. The small footprint and low price, make the Nano Every particularly suited for wearable inventions, low cost robotics, electronic musical instruments, and general use to control smaller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
  2 channel relay module: 2 channel Relay Module 5V 12V 24V High and Low Level Trigger Relay Control With Optocoupler Two Way relays DC 5 V 12 V 24 V Volt.
  LCD2004-I2C: A standard character display with 4x20 characters. Comes in many colors with LCM2004 IIC attached.
